// Logisim project logisimproject.circ as structural Verilog: 1 circuit, main circuit main
module main (
  input  A3,
  input  B3,
  input  A2,
  input  B2,
  input  A1,
  input  B1,
  input  A0,
  input  B0,
  output out_9
);

  wire undriven, undriven_2, undriven_3, undriven_4, xor_1_out, xor_2_out, xor_3_out, xor_4_out;

  xor xor_1 (xor_1_out, A3, B3);
  xor xor_2 (xor_2_out, A2, B2);
  xor xor_3 (xor_3_out, A1, B1);
  xor xor_4 (xor_4_out, A0, B0);
  LED led_1 (.in(xor_1_out));
  LED led_2 (.in(xor_2_out));
  LED led_3 (.in(xor_3_out));
  LED led_4 (.in(xor_4_out));
  or or_1 (out_9, undriven, undriven_2, undriven_3, undriven_4);
  LED led_5 (.in(out_9));

  // Notes on the sheet:
  //   LED1
  //   LED2
  //   LED3
  //   LED4
endmodule
